# Fritzing sketch blue_tomato_schematic (saved by Fritzing 0.9.3b)
breadboards: 1

parts:
  Onderdeel1 = Arduino Uno (Rev3)
  LED1 = RGB LED - (4 legs) [package="5 mm [THT]"]
  R1 = Resistor [tolerance=±5% resistance=220 package="0402 [SMD]"]
  R2 = Resistor [tolerance=±5% resistance=2.2k package="0402 [SMD]"]
  R3 = Resistor [tolerance=±5% resistance=2.2k package="0402 [SMD]"]
  S1 = Pushbutton [package="[SMD]"]
  R4 = Resistor [tolerance=±5% resistance=220 package="0402 [SMD]"]
  J1 = Basic Servo

nets:
  N1: Onderdeel1.D2, R1.Pin_1
  N2: Onderdeel1.D3_PWM, R3.Pin_1
  N3: Onderdeel1.D4, R2.Pin_1
  N4: Onderdeel1.D5_PWM, J1.pulse
  5V: Onderdeel1.5V, S1.Pin_1, S1.Pin_2, J1.vcc
  GND: Onderdeel1.GND, LED1.common_anode, R4.Pin_0, J1.gnd
  N5: LED1.red_cathode, R1.Pin_0
  N6: LED1.green_cathode, R3.Pin_0
  N7: LED1.blue_cathode, R2.Pin_0
  N8: S1.Pin_3, S1.Pin_4, R4.Pin_1
